// Logisim project Datapath Main.circ as structural Verilog: 9 circuits, main circuit main
module main (
  input  in_1,
  input  [15:0] In,
  input  Enter,
  input  in_4,
  output [15:0] out_5,
  output [15:0] out_6,
  output [11:0] out_7,
  output out_8,
  output [15:0] out_9,
  output [15:0] out_10,
  output [11:0] out_11,
  output [11:0] out_12
);

  wire ALU_Src, beq, Beq_out, bne, Bne_out, Clk_out, en, enter_value_slct_1_out_4, in_selector_1_clkout, j,
       main_1_p6, Mem_read, Mem_to_Reg, Mem_Write, not_1_out, out_control_1_a, out_control_1_b,
       out_control_1_c, out_control_1_d, out_control_1_e, out_control_1_f, out_control_1_g, out_control_2_a,
       out_control_2_b, out_control_2_c, out_control_2_d, out_control_2_e, out_control_2_f, out_control_2_g,
       out_control_3_a, out_control_3_b, out_control_3_c, out_control_3_d, out_control_3_e, out_control_3_f,
       out_control_3_g, out_control_4_a, out_control_4_b, out_control_4_c, out_control_4_d, out_control_4_e,
       out_control_4_f, out_control_4_g, reg_Dst, reg_Write, undriven, zero;
  wire [2:0] Opcode;
  wire [3:0] multiplexer_3_out;
  wire [11:0] adder_2_out, bit_extender_1_out, bit_extender_3_out, multiplexer_1_out, multiplexer_2_out,
       multiplexer_5_out, register_1_q, shifter_1_out;
  wire [15:0] controlled_buffer_1_out, controlled_buffer_2_out, ID, multiplexer_4_out, read_data1, Result;

  Clock Clk (.out(Clk_out));
  assign bit_extender_1_out = {{8{1'b0}}, out_5[3:0]};  // Bit_Extender bit_extender_1
  Multiplexer #(.width(12)) multiplexer_1 (
    .in0(out_12), .in1(bit_extender_1_out), .out(multiplexer_1_out), .sel(j));  // open: en
  Register #(.width(12)) register_1 (.D(multiplexer_1_out), .en(undriven), .Q(register_1_q), .clk(Clk_out), .clr(in_1));
  assign ID = {{12{1'b0}}, out_5[3:0]};  // Bit_Extender bit_extender_2
  In_selector in_selector_1 (
    .I3(out_5[15]), .I2(out_5[14]), .I1(out_5[13]), .I0(out_5[12]), .ClkOut(in_selector_1_clkout));
  Adder #(.width(12)) adder_1 (.a(register_1_q), .b(multiplexer_2_out), .out(out_11));  // open: cin, cout
  Multiplexer #(.width(12)) multiplexer_2 (
    .in0(12'h1), .in1({12{1'b0}}), .out(multiplexer_2_out), .sel(enter_value_slct_1_out_4));  // open: en
  Enter_Value_Slct enter_value_slct_1 (
    .zero(in_selector_1_clkout), .one(1'b0), .clk(Enter), .out_4(enter_value_slct_1_out_4));
  ROM #(.addrWidth(12), .dataWidth(16)) rom_1 (.addr(register_1_q), .data(out_5));  // open: sel
  assign controlled_buffer_1_out = Enter ? In : 16'bz;  // Controlled_Buffer controlled_buffer_1
  Multiplexer #(.width(4)) multiplexer_3 (
    .in0(out_5[3:0]), .in1(out_5[7:4]), .out(multiplexer_3_out), .sel(reg_Dst));  // open: en
  out_control out_control_1 (
    .o3(controlled_buffer_2_out[15]), .o2(controlled_buffer_2_out[14]), .o1(controlled_buffer_2_out[13]),
    .o0(controlled_buffer_2_out[12]), .a(out_control_1_a), .b(out_control_1_b), .c(out_control_1_c),
    .d(out_control_1_d), .e(out_control_1_e), .f(out_control_1_f), .g(out_control_1_g));
  _7_Segment_Display u_7_segment_display_1 (
    .g(out_control_1_g), .f(out_control_1_f), .a(out_control_1_a), .b(out_control_1_b), .e(out_control_1_e),
    .d(out_control_1_d), .c(out_control_1_c));  // open: dp
  out_control out_control_2 (
    .o3(controlled_buffer_2_out[11]), .o2(controlled_buffer_2_out[10]), .o1(controlled_buffer_2_out[9]),
    .o0(controlled_buffer_2_out[8]), .a(out_control_2_a), .b(out_control_2_b), .c(out_control_2_c),
    .d(out_control_2_d), .e(out_control_2_e), .f(out_control_2_f), .g(out_control_2_g));
  _7_Segment_Display u_7_segment_display_2 (
    .g(out_control_2_g), .f(out_control_2_f), .a(out_control_2_a), .b(out_control_2_b), .e(out_control_2_e),
    .d(out_control_2_d), .c(out_control_2_c));  // open: dp
  out_control out_control_3 (
    .o3(controlled_buffer_2_out[7]), .o2(controlled_buffer_2_out[6]), .o1(controlled_buffer_2_out[5]),
    .o0(controlled_buffer_2_out[4]), .a(out_control_3_a), .b(out_control_3_b), .c(out_control_3_c),
    .d(out_control_3_d), .e(out_control_3_e), .f(out_control_3_f), .g(out_control_3_g));
  _7_Segment_Display u_7_segment_display_3 (
    .g(out_control_3_g), .f(out_control_3_f), .a(out_control_3_a), .b(out_control_3_b), .e(out_control_3_e),
    .d(out_control_3_d), .c(out_control_3_c));  // open: dp
  register_w_in_out register_w_in_out_1 (
    .WriteData(Result), .RegWrite(reg_Write), .RdReg(multiplexer_3_out), .in_8(Clk_out),
    .in(controlled_buffer_1_out), .in_3(out_5[15:12]), .RdReg1(read_data1), .WriteReg1(out_5[11:8]),
    .RdReg2(out_9), .WriteReg2(out_5[7:4]));
  out_control out_control_4 (
    .o3(controlled_buffer_2_out[3]), .o2(controlled_buffer_2_out[2]), .o1(controlled_buffer_2_out[1]),
    .o0(controlled_buffer_2_out[0]), .a(out_control_4_a), .b(out_control_4_b), .c(out_control_4_c),
    .d(out_control_4_d), .e(out_control_4_e), .f(out_control_4_f), .g(out_control_4_g));
  _7_Segment_Display u_7_segment_display_4 (
    .g(out_control_4_g), .f(out_control_4_f), .a(out_control_4_a), .b(out_control_4_b), .e(out_control_4_e),
    .d(out_control_4_d), .c(out_control_4_c));  // open: dp
  Control_Unit control_unit_1 (
    .Op4(out_5[15]), .Op3(out_5[14]), .RegDst(reg_Dst), .Op2(out_5[13]), .Op1(out_5[12]), .ALUSrc(ALU_Src),
    .MemToReg(Mem_to_Reg), .RegWrite(reg_Write), .MemRead(Mem_read), .MemWrite(Mem_Write), .BranchBne(bne),
    .BranchBeq(beq), .ALUOp2(Opcode[2]), .ALUOp1(Opcode[1]), .ALUOp0(Opcode[0]), .Jump(j));
  Multiplexer #(.width(16)) multiplexer_4 (.in0(out_9), .in1(ID), .out(multiplexer_4_out), .sel(ALU_Src));  // open: en
  assign controlled_buffer_2_out = en ? read_data1 : 16'bz;  // Controlled_Buffer controlled_buffer_2
  assign bit_extender_3_out = {{8{1'b0}}, out_5[3:0]};  // Bit_Extender bit_extender_3
  // _16_bitALU__datapath__main main_1: pin names not known; wires that end beside it: read_data1, multiplexer_4_out, Opcode, out_6, zero, main_1_p6, out_8
  out_enable out_enable_1 (.I3(out_5[15]), .I2(out_5[14]), .I1(out_5[13]), .I0(out_5[12]), .O0(en));
  Shifter #(.width(12)) shifter_1 (.in(bit_extender_3_out), .\dist (4'b0000), .out(shifter_1_out));
  LED led_1 (.in(main_1_p6));
  not not_1 (not_1_out, zero);
  and u_Beq (Beq_out, zero, beq);
  Adder #(.width(12)) adder_2 (.a(out_11), .b(shifter_1_out), .out(adder_2_out));  // open: cin, cout
  and u_Bne (Bne_out, not_1_out, bne);
  Multiplexer #(.width(12)) multiplexer_5 (
    .in0(out_11), .in1(adder_2_out), .out(multiplexer_5_out), .sel(Beq_out));  // open: en
  RAM #(.addrWidth(16), .dataWidth(16), .bus("separate")) ram_1 (
    .addr(out_6), .din(out_9), .data(out_10), .str(Mem_Write), .clk(Clk_out), .ld(Mem_read), .clr(in_4));  // open: sel
  Multiplexer #(.width(12)) multiplexer_6 (
    .in0(multiplexer_5_out), .in1(adder_2_out), .out(out_12), .sel(Bne_out));  // open: en
  Multiplexer #(.width(16)) multiplexer_7 (.in0(out_6), .in1(out_10), .out(Result), .sel(Mem_to_Reg));  // open: en

  assign out_7 = out_5[11:0];

  // Other names for the same wires on the sheet: rd[3:0] = out_5[3:0]; Target[11:0] = out_5[11:0];
  //   rt[3:0] = out_5[7:4]; rs[3:0] = out_5[11:8]; OP[3:0] = out_5[15:12]; shift[11:0] = out_11;
  //   TargetPC[11:0] = out_12

  // Notes on the sheet:
  //   works
  //   works
  //   works
  //   works
  //   works
  //   works
  //   works
  //   works
  //   works
  //   works
  //   works
  //   works
  //   works
  //   works
  //   works
  //   Add
  //   sub
  //   and
  //   or
  //   nor
  //   sll
  //   srl
  //   jump
  //   addi
  //   lw
  //   sw
  //   in
  //   bne
  //   beq
  //   out
  //   0000 0001 0011 0010 
  //   0001 1101 1110 1111
  //   0010 0001 1010 1011
  //   0011 1010 1011 1100
  //   0100 0011 1001 1010
  //   0101 1011 0001 1010
  //   0110 1100 1101 1111
  //   1111 000000001010
  //   0111 1011 1100 1010 
  //   1000 1001 1010 1011
  //   1001 1001 1010 1011
  //   1010 0000 0101 0000
  //   1101 1010 1011 0101
  //   1100 1001 1010 0101
  //   1011 0101 0000 0000
  //   0132
  //   1cef
  //   21ab
  //   3abc
  //   439a
  //   5b1a
  //   6cdf
  //   f00a
  //   7bca
  //   89ab
  //   99ab
  //   a050
  //   dab5
  //   c9a5
  //   b500
  //   5a15
  //   99cb
  //   d9a2
  //   c9a2
  //   ba00
  //   contents of rom_1 (hex, n*v repeats v):
  //   8102 7bca a0a0 bb00 333 334 7221 f003 9304
endmodule

module in_control (
  input  [3:0] op,
  output m
);

  wire not_1_out, not_2_out;

  not not_1 (not_1_out, op[2]);
  not not_2 (not_2_out, op[0]);
  and and_1 (m, op[3], not_1_out, op[1], not_2_out);
endmodule

module register_w_in_out (
  input  [15:0] WriteData,
  input  [15:0] in,
  input  [3:0] in_3,
  input  RegWrite,
  input  [3:0] WriteReg1,
  input  [3:0] RdReg,
  input  [3:0] WriteReg2,
  input  in_8,
  output [15:0] RdReg1,
  output [15:0] RdReg2
);

  wire _0, _1, _2, _3, _4, _5, _6, _7, _8, _9, _10, _11, _12, _13, _14, _15, and_1_out, and_2_out, and_3_out,
       and_4_out, and_5_out, and_6_out, and_7_out, and_8_out, and_9_out, and_10_out, and_11_out, and_12_out,
       and_13_out, and_14_out, and_15_out, and_16_out, decoder_1_out0, decoder_1_out1, decoder_1_out2,
       decoder_1_out3, decoder_1_out4, decoder_1_out5, decoder_1_out6, decoder_1_out7, decoder_1_out8,
       decoder_1_out9, decoder_1_out10, decoder_1_out11, decoder_1_out12, decoder_1_out13, decoder_1_out14,
       decoder_1_out15, in_control_1_m, multiplexer_1_out, multiplexer_2_out, multiplexer_3_out,
       multiplexer_4_out, multiplexer_5_out, multiplexer_6_out, multiplexer_7_out, multiplexer_8_out,
       multiplexer_9_out, multiplexer_10_out, multiplexer_11_out, multiplexer_12_out, multiplexer_13_out,
       multiplexer_14_out, multiplexer_15_out, multiplexer_16_out;
  wire [15:0] multiplexer_17_out, register_1_q, register_2_q, register_3_q, register_4_q, register_5_q,
       register_6_q, register_7_q, register_8_q, register_9_q, register_10_q, register_11_q, register_12_q,
       register_13_q, register_14_q, register_15_q, register_16_q;

  Decoder #(.select(4)) decoder_1 (
    .out0(decoder_1_out0), .out1(decoder_1_out1), .out2(decoder_1_out2), .out3(decoder_1_out3),
    .out4(decoder_1_out4), .out5(decoder_1_out5), .out6(decoder_1_out6), .out7(decoder_1_out7),
    .out8(decoder_1_out8), .out9(decoder_1_out9), .out10(decoder_1_out10), .out11(decoder_1_out11),
    .out12(decoder_1_out12), .out13(decoder_1_out13), .out14(decoder_1_out14), .out15(decoder_1_out15),
    .sel(RdReg));  // open: en
  Multiplexer multiplexer_1 (
    .in0(decoder_1_out0), .in1(_0), .out(multiplexer_1_out), .sel(in_control_1_m));  // open: en
  Multiplexer multiplexer_2 (
    .in0(decoder_1_out1), .in1(_1), .out(multiplexer_2_out), .sel(in_control_1_m));  // open: en
  Multiplexer multiplexer_3 (
    .in0(decoder_1_out2), .in1(_2), .out(multiplexer_3_out), .sel(in_control_1_m));  // open: en
  Multiplexer multiplexer_4 (
    .in0(decoder_1_out3), .in1(_3), .out(multiplexer_4_out), .sel(in_control_1_m));  // open: en
  Multiplexer multiplexer_5 (
    .in0(decoder_1_out4), .in1(_4), .out(multiplexer_5_out), .sel(in_control_1_m));  // open: en
  Multiplexer multiplexer_6 (
    .in0(decoder_1_out5), .in1(_5), .out(multiplexer_6_out), .sel(in_control_1_m));  // open: en
  Multiplexer multiplexer_7 (
    .in0(decoder_1_out6), .in1(_6), .out(multiplexer_7_out), .sel(in_control_1_m));  // open: en
  Multiplexer multiplexer_8 (
    .in0(decoder_1_out7), .in1(_7), .out(multiplexer_8_out), .sel(in_control_1_m));  // open: en
  Multiplexer multiplexer_9 (
    .in0(decoder_1_out8), .in1(_8), .out(multiplexer_9_out), .sel(in_control_1_m));  // open: en
  Multiplexer multiplexer_10 (
    .in0(decoder_1_out9), .in1(_9), .out(multiplexer_10_out), .sel(in_control_1_m));  // open: en
  Multiplexer multiplexer_11 (
    .in0(decoder_1_out10), .in1(_10), .out(multiplexer_11_out), .sel(in_control_1_m));  // open: en
  Multiplexer multiplexer_12 (
    .in0(decoder_1_out11), .in1(_11), .out(multiplexer_12_out), .sel(in_control_1_m));  // open: en
  Multiplexer multiplexer_13 (
    .in0(decoder_1_out12), .in1(_12), .out(multiplexer_13_out), .sel(in_control_1_m));  // open: en
  Multiplexer multiplexer_14 (
    .in0(decoder_1_out13), .in1(_13), .out(multiplexer_14_out), .sel(in_control_1_m));  // open: en
  Multiplexer multiplexer_15 (
    .in0(decoder_1_out14), .in1(_14), .out(multiplexer_15_out), .sel(in_control_1_m));  // open: en
  Multiplexer multiplexer_16 (
    .in0(decoder_1_out15), .in1(_15), .out(multiplexer_16_out), .sel(in_control_1_m));  // open: en
  and and_1 (and_1_out, multiplexer_1_out, RegWrite);
  and and_2 (and_2_out, multiplexer_2_out, RegWrite);
  and and_3 (and_3_out, multiplexer_3_out, RegWrite);
  and and_4 (and_4_out, multiplexer_4_out, RegWrite);
  and and_5 (and_5_out, multiplexer_5_out, RegWrite);
  and and_6 (and_6_out, multiplexer_6_out, RegWrite);
  and and_7 (and_7_out, multiplexer_7_out, RegWrite);
  and and_8 (and_8_out, multiplexer_8_out, RegWrite);
  and and_9 (and_9_out, multiplexer_9_out, RegWrite);
  and and_10 (and_10_out, multiplexer_10_out, RegWrite);
  and and_11 (and_11_out, multiplexer_11_out, RegWrite);
  and and_12 (and_12_out, multiplexer_12_out, RegWrite);
  and and_13 (and_13_out, multiplexer_13_out, RegWrite);
  and and_14 (and_14_out, multiplexer_14_out, RegWrite);
  and and_15 (and_15_out, multiplexer_15_out, RegWrite);
  and and_16 (and_16_out, multiplexer_16_out, RegWrite);
  Multiplexer #(.width(16)) multiplexer_17 (
    .in0(WriteData), .in1(in), .out(multiplexer_17_out), .sel(in_control_1_m));  // open: en
  Register #(.width(16)) register_1 (.D({16{1'b0}}), .en(and_1_out), .Q(register_1_q), .clk(in_8));  // open: clr
  Register #(.width(16)) register_2 (
    .D(multiplexer_17_out), .en(and_2_out), .Q(register_2_q), .clk(in_8));  // open: clr
  Register #(.width(16)) register_3 (
    .D(multiplexer_17_out), .en(and_3_out), .Q(register_3_q), .clk(in_8));  // open: clr
  Register #(.width(16)) register_4 (
    .D(multiplexer_17_out), .en(and_4_out), .Q(register_4_q), .clk(in_8));  // open: clr
  Register #(.width(16)) register_5 (
    .D(multiplexer_17_out), .en(and_5_out), .Q(register_5_q), .clk(in_8));  // open: clr
  Register #(.width(16)) register_6 (
    .D(multiplexer_17_out), .en(and_6_out), .Q(register_6_q), .clk(in_8));  // open: clr
  Register #(.width(16)) register_7 (
    .D(multiplexer_17_out), .en(and_7_out), .Q(register_7_q), .clk(in_8));  // open: clr
  Register #(.width(16)) register_8 (
    .D(multiplexer_17_out), .en(and_8_out), .Q(register_8_q), .clk(in_8));  // open: clr
  Register #(.width(16)) register_9 (
    .D(multiplexer_17_out), .en(and_9_out), .Q(register_9_q), .clk(in_8));  // open: clr
  Register #(.width(16)) register_10 (
    .D(multiplexer_17_out), .en(and_10_out), .Q(register_10_q), .clk(in_8));  // open: clr
  Register #(.width(16)) register_11 (
    .D(multiplexer_17_out), .en(and_11_out), .Q(register_11_q), .clk(in_8));  // open: clr
  Register #(.width(16)) register_12 (
    .D(multiplexer_17_out), .en(and_12_out), .Q(register_12_q), .clk(in_8));  // open: clr
  Register #(.width(16)) register_13 (
    .D(multiplexer_17_out), .en(and_13_out), .Q(register_13_q), .clk(in_8));  // open: clr
  Register #(.width(16)) register_14 (
    .D(multiplexer_17_out), .en(and_14_out), .Q(register_14_q), .clk(in_8));  // open: clr
  Register #(.width(16)) register_15 (
    .D(multiplexer_17_out), .en(and_15_out), .Q(register_15_q), .clk(in_8));  // open: clr
  Register #(.width(16)) register_16 (
    .D(multiplexer_17_out), .en(and_16_out), .Q(register_16_q), .clk(in_8));  // open: clr
  in_control in_control_1 (.op(in_3), .m(in_control_1_m));
  Multiplexer #(.select(4), .width(16)) multiplexer_18 (
    .in0(register_1_q), .in1(register_2_q), .in2(register_3_q), .in3(register_4_q), .in4(register_5_q),
    .in5(register_6_q), .in6(register_7_q), .in7(register_8_q), .in8(register_9_q), .in9(register_10_q),
    .in10(register_11_q), .in11(register_12_q), .in12(register_13_q), .in13(register_14_q),
    .in14(register_15_q), .in15(register_16_q), .out(RdReg1), .sel(WriteReg1));  // open: en
  Multiplexer #(.select(4), .width(16)) multiplexer_19 (
    .in0(register_1_q), .in1(register_2_q), .in2(register_3_q), .in3(register_4_q), .in4(register_5_q),
    .in5(register_6_q), .in6(register_7_q), .in7(register_8_q), .in8(register_9_q), .in9(register_10_q),
    .in10(register_11_q), .in11(register_12_q), .in12(register_13_q), .in13(register_14_q),
    .in14(register_15_q), .in15(register_16_q), .out(RdReg2), .sel(WriteReg2));  // open: en
  Decoder #(.select(4)) decoder_2 (
    .out0(_0), .out1(_1), .out2(_2), .out3(_3), .out4(_4), .out5(_5), .out6(_6), .out7(_7), .out8(_8),
    .out9(_9), .out10(_10), .out11(_11), .out12(_12), .out13(_13), .out14(_14), .out15(_15), .sel(WriteReg2));  // open: en

  // Notes on the sheet:
  //   rd
  //   0
  //   1
  //   2
  //   3
  //   4
  //   5
  //   6
  //   7
  //   8
  //   9
  //   10
  //   11
  //   12
  //   13
  //   14
  //   15
  //   rt
  //   rs
endmodule

module out_control (
  input  o3,
  input  o2,
  input  o1,
  input  o0,
  output a,
  output b,
  output c,
  output d,
  output e,
  output f,
  output g
);

  wire and_1_out, and_2_out, and_3_out, and_4_out, and_5_out, and_6_out, and_7_out, and_8_out, and_9_out,
       and_10_out, and_11_out, and_12_out, and_13_out, and_14_out, and_15_out, and_16_out, and_17_out,
       and_18_out, and_19_out, and_20_out, and_21_out, and_22_out, and_23_out, and_24_out, and_25_out,
       and_26_out, and_27_out, and_28_out, and_29_out, and_30_out, and_31_out, and_32_out, and_33_out,
       and_34_out, and_35_out, and_36_out, not_1_out, not_2_out, not_3_out, not_4_out, not_5_out, not_6_out,
       not_7_out, not_8_out, not_9_out, not_10_out, not_11_out, not_12_out, not_13_out, not_14_out,
       not_15_out, not_16_out, not_17_out, not_18_out, not_19_out, not_20_out, not_21_out, not_22_out,
       not_23_out, not_24_out, not_25_out, not_26_out, not_27_out, not_28_out, not_29_out, not_30_out,
       not_31_out, not_32_out, not_33_out, not_34_out, not_35_out, not_36_out, not_37_out, not_38_out,
       not_39_out, not_40_out, not_41_out, not_42_out, not_43_out;

  not not_1 (not_1_out, o2);
  and and_1 (and_1_out, not_1_out, not_2_out);
  not not_2 (not_2_out, o0);
  not not_3 (not_3_out, o3);
  and and_2 (and_2_out, not_3_out, o1);
  not not_4 (not_4_out, o3);
  and and_3 (and_3_out, not_4_out, o2, o0);
  and and_4 (and_4_out, o2, o1);
  and and_5 (and_5_out, o3, not_5_out, not_6_out);
  not not_5 (not_5_out, o2);
  not not_6 (not_6_out, o1);
  and and_6 (and_6_out, o3, not_7_out);
  not not_7 (not_7_out, o0);
  not not_8 (not_8_out, o3);
  and and_7 (and_7_out, not_8_out, not_9_out);
  not not_9 (not_9_out, o2);
  not not_10 (not_10_out, o3);
  not not_11 (not_11_out, o1);
  and and_8 (and_8_out, not_10_out, not_11_out, not_12_out);
  not not_12 (not_12_out, o0);
  not not_13 (not_13_out, o2);
  and and_9 (and_9_out, not_13_out, not_14_out);
  not not_14 (not_14_out, o1);
  not not_15 (not_15_out, o3);
  and and_10 (and_10_out, not_15_out, o1, o0);
  not not_16 (not_16_out, o1);
  and and_11 (and_11_out, o3, not_16_out, o0);
  and and_12 (and_12_out, o3, o1, not_17_out);
  not not_17 (not_17_out, o0);
  not not_18 (not_18_out, o3);
  and and_13 (and_13_out, not_18_out, not_19_out);
  not not_19 (not_19_out, o1);
  not not_20 (not_20_out, o3);
  and and_14 (and_14_out, not_20_out, o0);
  not not_21 (not_21_out, o1);
  and and_15 (and_15_out, not_21_out, o0);
  not not_22 (not_22_out, o3);
  and and_16 (and_16_out, not_22_out, o2);
  and and_17 (and_17_out, o3, not_23_out);
  not not_23 (not_23_out, o2);
  not not_24 (not_24_out, o2);
  and and_18 (and_18_out, not_24_out, not_25_out);
  not not_25 (not_25_out, o0);
  not not_26 (not_26_out, o2);
  and and_19 (and_19_out, not_26_out, o1);
  and and_20 (and_20_out, o1, not_27_out);
  not not_27 (not_27_out, o0);
  not not_28 (not_28_out, o1);
  and and_21 (and_21_out, o2, not_28_out, o0);
  and and_22 (and_22_out, o3, not_29_out);
  not not_29 (not_29_out, o1);
  not not_30 (not_30_out, o2);
  and and_23 (and_23_out, not_30_out, not_31_out);
  not not_31 (not_31_out, o0);
  and and_24 (and_24_out, o1, not_32_out);
  not not_32 (not_32_out, o0);
  and and_25 (and_25_out, o3, o1);
  and and_26 (and_26_out, o3, o2);
  not not_33 (not_33_out, o1);
  and and_27 (and_27_out, not_33_out, not_34_out);
  not not_34 (not_34_out, o0);
  not not_35 (not_35_out, o3);
  and and_28 (and_28_out, not_35_out, o2, not_36_out);
  not not_36 (not_36_out, o1);
  and and_29 (and_29_out, o2, not_37_out);
  not not_37 (not_37_out, o0);
  not not_38 (not_38_out, o2);
  and and_30 (and_30_out, o3, not_38_out, o0);
  and and_31 (and_31_out, o3, o2, o1);
  not not_39 (not_39_out, o2);
  and and_32 (and_32_out, not_39_out, o1);
  and and_33 (and_33_out, o1, not_40_out);
  not not_40 (not_40_out, o0);
  not not_41 (not_41_out, o3);
  and and_34 (and_34_out, not_41_out, o2, not_42_out);
  not not_42 (not_42_out, o1);
  and and_35 (and_35_out, o3, not_43_out);
  not not_43 (not_43_out, o2);
  and and_36 (and_36_out, o3, o0);
  or or_1 (c, and_13_out, and_14_out, and_15_out, and_16_out, and_17_out);
  or or_2 (d, and_18_out, and_19_out, and_20_out, and_21_out, and_22_out);
  or or_3 (e, and_23_out, and_24_out, and_25_out, and_26_out);
  or or_4 (f, and_27_out, and_28_out, and_29_out, and_30_out, and_31_out);
  or or_5 (g, and_32_out, and_33_out, and_34_out, and_35_out, and_36_out);
  or or_6 (a, and_1_out, and_2_out, and_3_out, and_4_out, and_5_out, and_6_out);
  or or_7 (b, and_7_out, and_8_out, and_9_out, and_10_out, and_11_out, and_12_out);
endmodule

module Control_Unit (
  input  Op4,
  input  Op3,
  input  Op2,
  input  Op1,
  output RegDst,
  output ALUSrc,
  output MemToReg,
  output RegWrite,
  output MemRead,
  output MemWrite,
  output BranchBne,
  output BranchBeq,
  output ALUOp2,
  output ALUOp1,
  output ALUOp0,
  output Jump
);

  wire and_1_out, and_2_out, and_4_out, and_5_out, and_6_out, and_7_out, and_9_out, and_10_out, and_11_out,
       and_12_out, and_13_out, and_14_out, and_17_out, and_18_out, and_19_out, and_20_out, and_21_out,
       and_22_out, and_23_out, and_24_out, not_1_out, not_2_out, not_3_out, not_4_out, not_5_out, not_6_out,
       not_7_out, not_8_out, not_9_out, not_10_out, not_11_out, not_12_out, not_13_out, not_14_out,
       not_15_out, not_16_out, not_17_out, not_18_out, not_19_out, not_20_out, not_21_out, not_22_out,
       not_23_out, not_24_out, not_25_out, not_26_out, not_27_out, not_28_out, not_29_out, not_30_out,
       not_31_out, not_32_out, not_33_out, not_34_out, not_35_out;

  not not_1 (not_1_out, Op4);
  not not_2 (not_2_out, Op3);
  and and_1 (and_1_out, Op3, Op2, Op1);
  and and_2 (and_2_out, Op4, not_3_out);
  not not_3 (not_3_out, Op3);
  and and_3 (MemToReg, Op4, not_4_out);
  not not_4 (not_4_out, Op3);
  not not_5 (not_5_out, Op4);
  not not_6 (not_6_out, Op3);
  and and_4 (and_4_out, not_6_out, not_7_out);
  not not_7 (not_7_out, Op1);
  not not_8 (not_8_out, Op3);
  and and_5 (and_5_out, not_8_out, Op2);
  not not_9 (not_9_out, Op3);
  not not_10 (not_10_out, Op2);
  not not_11 (not_11_out, Op1);
  not not_12 (not_12_out, Op3);
  not not_13 (not_13_out, Op3);
  not not_14 (not_14_out, Op2);
  not not_15 (not_15_out, Op3);
  not not_16 (not_16_out, Op1);
  not not_17 (not_17_out, Op2);
  not not_18 (not_18_out, Op2);
  not not_19 (not_19_out, Op1);
  not not_20 (not_20_out, Op4);
  and and_6 (and_6_out, not_20_out, Op3, not_21_out);
  not not_21 (not_21_out, Op2);
  not not_22 (not_22_out, Op4);
  and and_7 (and_7_out, not_22_out, Op3, not_23_out);
  not not_23 (not_23_out, Op1);
  not not_24 (not_24_out, Op3);
  not not_25 (not_25_out, Op2);
  not not_26 (not_26_out, Op2);
  not not_27 (not_27_out, Op1);
  not not_28 (not_28_out, Op4);
  not not_29 (not_29_out, Op3);
  not not_30 (not_30_out, Op2);
  not not_31 (not_31_out, Op4);
  not not_32 (not_32_out, Op3);
  not not_33 (not_33_out, Op4);
  not not_34 (not_34_out, Op1);
  not not_35 (not_35_out, Op2);
  and and_8 (Jump, Op4, Op3, Op2, Op1);
  and and_9 (and_9_out, not_1_out, Op3, Op2, Op1);
  or or_1 (RegDst, and_9_out, and_10_out);
  and and_10 (and_10_out, Op4, not_2_out);
  or or_2 (ALUSrc, and_1_out, and_2_out);
  or or_3 (RegWrite, not_5_out, and_4_out, and_5_out);
  and and_11 (and_11_out, Op4, not_9_out, not_10_out, not_11_out);
  or or_4 (MemRead, and_11_out, and_12_out);
  and and_12 (and_12_out, Op4, not_12_out, Op2, Op1);
  and and_13 (and_13_out, Op4, not_13_out, not_14_out, Op1);
  or or_5 (MemWrite, and_13_out, and_14_out);
  and and_14 (and_14_out, Op4, not_15_out, Op2, not_16_out);
  and and_15 (BranchBne, Op4, Op3, not_17_out, Op1);
  and and_16 (BranchBeq, Op4, Op3, not_18_out, not_19_out);
  or or_6 (ALUOp2, and_6_out, and_7_out);
  and and_17 (and_17_out, not_24_out, not_25_out);
  and and_18 (and_18_out, not_26_out, not_27_out);
  and and_19 (and_19_out, not_28_out, Op3, Op2, Op1);
  and and_20 (and_20_out, Op4, not_29_out);
  and and_21 (and_21_out, Op4, not_30_out);
  and and_22 (and_22_out, not_31_out, not_32_out, Op1);
  or or_7 (ALUOp0, and_22_out, and_23_out, and_24_out);
  and and_23 (and_23_out, not_33_out, Op3, Op2, not_34_out);
  and and_24 (and_24_out, Op4, Op3, not_35_out);
  or or_8 (ALUOp1, and_17_out, and_18_out, and_19_out, and_20_out, and_21_out);
endmodule

module beq_bne_mux (
  input  I3,
  input  I2,
  input  I1,
  input  I0,
  input  ZeroSig,
  output O0
);

  wire and_1_out, and_2_out, not_1_out, not_2_out, not_3_out, not_4_out;

  not not_1 (not_1_out, I1);
  not not_2 (not_2_out, I0);
  not not_3 (not_3_out, I1);
  not not_4 (not_4_out, ZeroSig);
  and and_1 (and_1_out, I3, I2, not_1_out, not_2_out, ZeroSig);
  and and_2 (and_2_out, I3, I2, not_3_out, I0, not_4_out);
  or or_1 (O0, and_1_out, and_2_out);
endmodule

module out_enable (
  input  I3,
  input  I2,
  input  I1,
  input  I0,
  output O0
);

  wire not_1_out;

  not not_1 (not_1_out, I2);
  and and_1 (O0, I3, not_1_out, I1, I0);
endmodule

module In_selector (
  input  I3,
  input  I2,
  input  I1,
  input  I0,
  output ClkOut
);

  wire not_1_out, not_2_out;

  not not_1 (not_1_out, I2);
  not not_2 (not_2_out, I0);
  and and_1 (ClkOut, I3, not_1_out, I1, not_2_out);
endmodule

module Enter_Value_Slct (
  input  zero,
  input  one,
  input  clk,
  output out_4
);

  Multiplexer multiplexer_1 (.in0(zero), .in1(one), .out(out_4), .sel(clk));  // open: en
endmodule
